# Fritzing sketch ProMicroMatrixLed (saved by Fritzing 0.9.3b)

parts:
  Pro_Micro1 = Pro Micro
  Componente1 = Matrix LED de 8x8 basada en MAX7219
  VCC1 = Battery

nets:
  N1: Pro_Micro1.GND#3, VCC1.-
  N2: Pro_Micro1.D2, Componente1.DIN
  N3: Pro_Micro1.D3, Componente1.CS
  N4: Pro_Micro1.D4, Componente1.CLK
  VCC: Pro_Micro1.VCC, Componente1.VCC
  N5: Pro_Micro1.GND#23, Componente1.GND
  N6: Pro_Micro1.RAW, VCC1.+

custom parts:
  Pro Micro: The SparkFun Pro Micro is a complete USB-based microcontoller development system, in a very small footprint, capable of implementing many types of projects. All programming can be done via the USB port.
